# Fritzing sketch Hardware (saved by Fritzing 0.9.10b)
breadboards: 1

parts:
  Mod1 = Amica NodeMCU DEVKIT 1.0
  DHT1 = DHT11 Humitidy and Temperature Sensor (3 pins)
  LED1 = LED - 5mm [color="Red (633nm)" current=0.030 package="5 mm [THT]"]
  LED2 = LED - 5mm [color="Yellow (595nm)" current=0.030 package="5 mm [THT]"]
  M1 = 1 chan 5v relay module
  F1 = Fan - Ventilador [package=THT]
  Power_plug1 = Power plug
  R1 = PHOTOCELL [package=photocell-kit]
  R2 = Resistor [tolerance=±5% resistance=220 package="2512 [SMD]"]
  R3 = Resistor [tolerance=±5% resistance=220 package="2512 [SMD]"]
  R4 = Resistor [tolerance=±5% power=0.25 resistance=220 package=THT]
  J1 = Piezo Speaker

nets:
  N1: Mod1.pin1, Mod1.pin_10, Mod1.pin_26, DHT1.Plus, DHT1.Gnd, R1.P$2
  N2: Mod1.pin2, Mod1.pin_9, Mod1.pin_25, Mod1.pin_29, LED1.cathode, LED2.cathode, M1.pin_2, F1.GND, R4.Pin_0
  N3: Mod1.pin6, DHT1.Signal
  N4: Mod1.pin_12, R2.Pin_0
  N5: Mod1.pin_13, R3.Pin_0
  N6: Mod1.pin_14, M1.pin_3
  N7: Mod1.pin_16, R1.P$1, R4.Pin_1
  N8: Mod1.pin_30, M1.pin_1, F1.5V
  N9: LED1.anode, R3.Pin_1
  N10: LED2.anode, R2.Pin_1
  N11: M1.pin_5, Power_plug1.VCC
  N12: M1.pin_6, J1.pin1
  N13: Power_plug1.GND, J1.pin2

custom parts:
  DHT11 Humitidy and Temperature Sensor (3 pins): DHT11 Humidity and Temperature Sensor (3 pins).
  1 chan 5v relay module: 1 Channel 5V Relay Module Board Shield with Optocoupler Support High and Low Level Trigger for Arduino.
  Fan - Ventilador: Ventilador de 2 pines, se encuentra comunmente en computadoras de escritorio
